# Fritzing sketch Stepper motor wiring (saved by Fritzing 0.9.0b)
breadboards: 2

parts:
  IC1 = ULN2003A [package="SO16 [SMD]"]
  부품2 = Arduino Mega 2560 (Rev3)
  LED1 = LED - 5mm [color="Red (633nm)" package="5 mm [THT]"]
  LED2 = LED - 5mm [color="Red (633nm)" package="5 mm [THT]"]
  LED3 = LED - 5mm [color="Red (633nm)" package="5 mm [THT]"]
  LED4 = LED - 5mm [color="Red (633nm)" package="5 mm [THT]"]

nets:
  N1: IC1.In_1, 부품2.D2_PWM, LED1.anode
  N2: IC1.In_3, 부품2.D4_PWM, LED2.anode
  N3: IC1.In_4, 부품2.D5_PWM, LED3.anode
  N4: IC1.In_6, 부품2.D3_PWM, LED4.anode
  N5: IC1.0V, 부품2.GND, LED1.cathode, LED2.cathode, LED3.cathode, LED4.cathode
  N6: IC1.COM_-_Common, 부품2.5V
